// Logisim project SRAM_Cell_circuit.circ as structural Verilog: 1 circuit, main circuit main
module main (
  input  WL,
  input  BL,
  input  BL_bar
);

  wire ACCESS1_out, ACCESS2_out, NAND1_out, NAND2_out;

  nand ACCESS1 (ACCESS1_out, WL, BL_bar);
  nand ACCESS2 (ACCESS2_out, WL, BL);
  nand NAND1 (NAND1_out, ACCESS1_out, NAND2_out);
  LED Q (.in(NAND1_out));
  LED Q_bar (.in(NAND2_out));
  nand NAND2 (NAND2_out, NAND1_out, ACCESS2_out);
endmodule
